# Fritzing sketch BOARD-V-2019-04-25 (saved by Fritzing 0.9.3b)

parts:
  Raspberry_Pi_2 = Raspberry Pi 3 [part_number=RPI-3-V1.2]
  SLOT8 = Lilypad Battery Connect
  SLOT5 = Lilypad Battery Connect
  SLOT6 = Lilypad Battery Connect  # not connected
  SLOT7 = Lilypad Battery Connect  # not connected
  SLOT1 = Lilypad Battery Connect
  SLOT3 = Lilypad Battery Connect  # not connected
  SLOT4 = Lilypad Battery Connect
  SLOT2 = Lilypad Battery Connect  # not connected
  Part25 = Lilypad Battery Connect
  Part26 = Lilypad Battery Connect
  Part27 = Lilypad Battery Connect
  Part28 = Lilypad Battery Connect
  Part29 = Lilypad Battery Connect
  Part30 = Lilypad Battery Connect
  Part31 = Lilypad Battery Connect
  Part32 = Lilypad Battery Connect
  IC2 = ULN2003A [package="DIP16 [THT]"]
  33k = Resistor [tolerance=±1% resistance=1k package=THT]
  220k = Resistor [tolerance=±1% resistance=1k package=THT]
  100k = Resistor [tolerance=±1% resistance=1k package=THT]
  22k = Resistor [tolerance=±1% resistance=1k package=THT]
  10k = Resistor [tolerance=±1% resistance=1k package=THT]
  220k_2 = Resistor [tolerance=±1% resistance=1k package=THT]
  470k = Resistor [tolerance=±1% resistance=1k package=THT]
  100k_2 = Resistor [tolerance=±1% resistance=1k package=THT]
  330k = Resistor [tolerance=±1% resistance=1k package=THT]
  330k_2 = Resistor [tolerance=±1% resistance=1k package=THT]
  470k_2 = Resistor [tolerance=±1% resistance=1k package=THT]
  10k_2 = Resistor [tolerance=±1% resistance=1k package=THT]
  22k_2 = Resistor [tolerance=±1% resistance=1k package=THT]
  47k = Resistor [tolerance=±1% resistance=1k package=THT]
  47k_2 = Resistor [tolerance=±1% resistance=1k package=THT]
  33k_2 = Resistor [tolerance=±1% resistance=1k package=THT]
  Part33 = Arduino Color LCD Shield  # not connected
  IC3 = ULN2003A [package="DIP16 [THT]"]
  4_7k = Resistor [tolerance=±1% resistance=1k package=THT]
  4_7k_2 = Resistor [tolerance=±1% resistance=1k package=THT]
  4_7k_3 = Resistor [tolerance=±1% resistance=1k package=THT]
  4_7k_4 = Resistor [tolerance=±1% resistance=1k package=THT]
  4_7k_5 = Resistor [tolerance=±1% resistance=1k package=THT]
  4_7k_6 = Resistor [tolerance=±1% resistance=1k package=THT]
  4_7k_7 = Resistor [tolerance=±1% resistance=1k package=THT]
  4_7k_8 = Resistor [tolerance=±1% resistance=1k package=THT]
  SLOT9 = Lilypad Battery Connect  # not connected
  Part35 = Lilypad Battery Connect
  4_7k_9 = Resistor [tolerance=±1% resistance=1k package=THT]

nets:
  N1: Raspberry_Pi_2.3v3, IC2.Out_1
  N2: Raspberry_Pi_2.GND, IC2.Out_3, 33k.Pin_1, 100k.Pin_1, 220k_2.Pin_1, 470k.Pin_1, 330k_2.Pin_1, 10k_2.Pin_1, 22k_2.Pin_1, 47k_2.Pin_1
  N3: Raspberry_Pi_2.GIPO17, IC2.Out_7
  N4: Raspberry_Pi_2.GIPO27, IC3.Out_7
  N5: Raspberry_Pi_2.GIPO24, IC3.Out_6
  N6: Raspberry_Pi_2.GIPO23, IC2.Out_5
  N7: Raspberry_Pi_2.GIPO18, IC2.Out_4
  N8: SLOT8.+, IC2.0V, 470k.Pin_0
  N9: SLOT5.+, IC2.In_5, 100k.Pin_0
  N10: SLOT1.+, 10k_2.Pin_0
  N11: SLOT4.+, IC2.In_4, 47k_2.Pin_0
  N12: Part25.-, 470k_2.Pin_1
  N13: Part25.+, 470k_2.Pin_0
  N14: Part26.-, 100k_2.Pin_1
  N15: Part26.+, 100k_2.Pin_0
  N16: Part27.-, 220k.Pin_1
  N17: Part27.+, 220k.Pin_0
  N18: Part28.-, 330k.Pin_1
  N19: Part28.+, 330k.Pin_0
  N20: Part29.-, 10k.Pin_1
  N21: Part29.+, 10k.Pin_0
  N22: Part30.-, 33k_2.Pin_1
  N23: Part30.+, 33k_2.Pin_0
  N24: Part31.-, 47k.Pin_1
  N25: Part31.+, 47k.Pin_0
  N26: Part32.-, 22k.Pin_1
  N27: Part32.+, 22k.Pin_0
  N28: IC2.In_2, 22k_2.Pin_0
  N29: IC2.In_3, 33k.Pin_0
  N30: IC2.In_6, 220k_2.Pin_0
  N31: IC2.In_7, 330k_2.Pin_0
  N32: IC3.In_1, 4_7k.Pin_0
  N33: IC3.In_2, 4_7k_2.Pin_0
  N34: IC3.In_3, 4_7k_3.Pin_0
  N35: IC3.In_4, 4_7k_4.Pin_0
  N36: IC3.In_5, 4_7k_5.Pin_0
  N37: IC3.In_6, 4_7k_6.Pin_0
  N38: IC3.In_7, 4_7k_7.Pin_0
  N39: IC3.0V, 4_7k_8.Pin_0
  N40: Part35.-, 4_7k_9.Pin_1
  N41: Part35.+, 4_7k_9.Pin_0
