# Fritzing sketch CIRCLE-v2019-04-25 (saved by Fritzing 0.9.3b)

parts:
  IC1 = ULN2003A [package="DIP16 [THT]"]
  SLOT10 = Lilypad Battery Connect  # not connected
  SLOT9 = Lilypad Battery Connect
  33k = Resistor [tolerance=±1% resistance=1k package=THT]
  33k_2 = Resistor [tolerance=±1% resistance=1k package=THT]  # not connected
  33k_3 = Resistor [tolerance=±1% resistance=1k package=THT]
  33k_4 = Resistor [tolerance=±1% resistance=1k package=THT]
  33k_5 = Resistor [tolerance=±1% resistance=1k package=THT]
  33k_6 = Resistor [tolerance=±1% resistance=1k package=THT]
  33k_7 = Resistor [tolerance=±1% resistance=1k package=THT]
  33k_8 = Resistor [tolerance=±1% resistance=1k package=THT]
  Part10 = Lilypad Battery Connect
  Part11 = Lilypad Battery Connect
  Part12 = Lilypad Battery Connect
  Part13 = Lilypad Battery Connect
  Part14 = Lilypad Battery Connect
  Part15 = Lilypad Battery Connect
  Part16 = Lilypad Battery Connect
  10k = Resistor [tolerance=±1% resistance=1k package=THT]
  10k_2 = Resistor [tolerance=±1% resistance=1k package=THT]
  100k = Resistor [tolerance=±1% resistance=1k package=THT]
  100k_2 = Resistor [tolerance=±1% resistance=1k package=THT]
  10k_3 = Resistor [tolerance=±1% resistance=1k package=THT]
  10k_4 = Resistor [tolerance=±1% resistance=1k package=THT]
  10k_5 = Resistor [tolerance=±1% resistance=1k package=THT]
  Raspberry_Pi_2 = Raspberry Pi 3 [part_number=RPI-3-V1.2]
  SLOT8 = Lilypad Battery Connect
  SLOT5 = Lilypad Battery Connect
  SLOT6 = Lilypad Battery Connect  # not connected
  SLOT7 = Lilypad Battery Connect  # not connected
  SLOT1 = Lilypad Battery Connect
  SLOT3 = Lilypad Battery Connect  # not connected
  SLOT4 = Lilypad Battery Connect
  SLOT2 = Lilypad Battery Connect  # not connected
  Part25 = Lilypad Battery Connect
  Part26 = Lilypad Battery Connect
  Part27 = Lilypad Battery Connect
  Part28 = Lilypad Battery Connect
  Part29 = Lilypad Battery Connect
  Part30 = Lilypad Battery Connect
  Part31 = Lilypad Battery Connect
  Part32 = Lilypad Battery Connect
  IC2 = ULN2003A [package="DIP16 [THT]"]
  33k_9 = Resistor [tolerance=±1% resistance=1k package=THT]
  100k_3 = Resistor [tolerance=±1% resistance=1k package=THT]
  33k_10 = Resistor [tolerance=±1% resistance=1k package=THT]
  33k_11 = Resistor [tolerance=±1% resistance=1k package=THT]
  33k_12 = Resistor [tolerance=±1% resistance=1k package=THT]
  33k_13 = Resistor [tolerance=±1% resistance=1k package=THT]
  33k_14 = Resistor [tolerance=±1% resistance=1k package=THT]
  33k_15 = Resistor [tolerance=±1% resistance=1k package=THT]
  100k_4 = Resistor [tolerance=±1% resistance=1k package=THT]
  33k_16 = Resistor [tolerance=±1% resistance=1k package=THT]
  33k_17 = Resistor [tolerance=±1% resistance=1k package=THT]
  33k_18 = Resistor [tolerance=±1% resistance=1k package=THT]
  33k_19 = Resistor [tolerance=±1% resistance=1k package=THT]
  33k_20 = Resistor [tolerance=±1% resistance=1k package=THT]
  33k_21 = Resistor [tolerance=±1% resistance=1k package=THT]
  100k_5 = Resistor [tolerance=±1% resistance=1k package=THT]
  Part33 = Arduino Color LCD Shield  # not connected

nets:
  N1: IC1.In_1, SLOT9.+, 33k.Pin_0
  N2: IC1.In_3, 33k_3.Pin_0
  N3: IC1.In_4, 33k_4.Pin_0
  N4: IC1.In_5, 33k_5.Pin_0
  N5: IC1.In_6, 33k_6.Pin_0
  N6: IC1.In_7, 33k_7.Pin_0
  N7: IC1.0V, 33k_8.Pin_0
  N8: IC1.Out_7, Raspberry_Pi_2.GIPO27
  N9: IC1.Out_3, Raspberry_Pi_2.GND, IC2.Out_3, 33k_9.Pin_1, 33k_10.Pin_1, 33k_13.Pin_1, 33k_14.Pin_1, 33k_16.Pin_1, 33k_17.Pin_1, 33k_18.Pin_1, 33k_20.Pin_1
  N10: 33k.Pin_1, 33k_8.Pin_1
  N11: Part10.-, 10k_4.Pin_1
  N12: Part10.+, 10k_4.Pin_0
  N13: Part11.-, 10k.Pin_1
  N14: Part11.+, 10k.Pin_0
  N15: Part12.-, 10k_5.Pin_1
  N16: Part12.+, 10k_5.Pin_0
  N17: Part13.-, 100k.Pin_1
  N18: Part13.+, 100k.Pin_0
  N19: Part14.-, 10k_3.Pin_1
  N20: Part14.+, 10k_3.Pin_0
  N21: Part15.-, 10k_2.Pin_1
  N22: Part15.+, 10k_2.Pin_0
  N23: Part16.-, 100k_2.Pin_1
  N24: Part16.+, 100k_2.Pin_0
  N25: Raspberry_Pi_2.3v3, IC2.Out_1
  N26: Raspberry_Pi_2.GIPO17, IC2.Out_7
  N27: Raspberry_Pi_2.GIPO24, IC2.Out_6
  N28: Raspberry_Pi_2.GIPO23, IC2.Out_5
  N29: Raspberry_Pi_2.GIPO15, IC2.Out_4
  N30: SLOT8.+, IC2.0V, 33k_14.Pin_0
  N31: SLOT5.+, IC2.In_5, 33k_10.Pin_0
  N32: SLOT1.+, IC2.In_1, 33k_17.Pin_0
  N33: SLOT4.+, IC2.In_4, 33k_20.Pin_0
  N34: Part25.-, 100k_5.Pin_1
  N35: Part25.+, 100k_5.Pin_0
  N36: Part26.-, 33k_15.Pin_1
  N37: Part26.+, 33k_15.Pin_0
  N38: Part27.-, 100k_3.Pin_1
  N39: Part27.+, 100k_3.Pin_0
  N40: Part28.-, 100k_4.Pin_1
  N41: Part28.+, 100k_4.Pin_0
  N42: Part29.-, 33k_12.Pin_1
  N43: Part29.+, 33k_12.Pin_0
  N44: Part30.-, 33k_21.Pin_1
  N45: Part30.+, 33k_21.Pin_0
  N46: Part31.-, 33k_19.Pin_1
  N47: Part31.+, 33k_19.Pin_0
  N48: Part32.-, 33k_11.Pin_1
  N49: Part32.+, 33k_11.Pin_0
  N50: IC2.In_2, 33k_18.Pin_0
  N51: IC2.In_3, 33k_9.Pin_0
  N52: IC2.In_6, 33k_13.Pin_0
  N53: IC2.In_7, 33k_16.Pin_0

notes:
  KLOCKI
  SLOTY
  LCD
