# Fritzing sketch MASLOW-V-2019-04-25 (saved by Fritzing 0.9.3b)

parts:
  Raspberry_Pi_2 = Raspberry Pi 3 [part_number=RPI-3-V1.2]
  SLOT8 = Lilypad Battery Connect
  SLOT5 = Lilypad Battery Connect
  SLOT6 = Lilypad Battery Connect  # not connected
  SLOT7 = Lilypad Battery Connect  # not connected
  SLOT1 = Lilypad Battery Connect
  SLOT3 = Lilypad Battery Connect  # not connected
  SLOT4 = Lilypad Battery Connect
  SLOT2 = Lilypad Battery Connect  # not connected
  Part25 = Lilypad Battery Connect
  Part26 = Lilypad Battery Connect
  Part28 = Lilypad Battery Connect
  Part29 = Lilypad Battery Connect
  Part30 = Lilypad Battery Connect
  Part31 = Lilypad Battery Connect
  Part32 = Lilypad Battery Connect
  IC2 = ULN2003A [package="DIP16 [THT]"]
  4_7k = Resistor [tolerance=±1% resistance=1k package=THT]
  4_7k_2 = Resistor [tolerance=±1% resistance=1k package=THT]
  4_7k_3 = Resistor [tolerance=±1% resistance=1k package=THT]
  4_7k_4 = Resistor [tolerance=±1% resistance=1k package=THT]
  4_7k_5 = Resistor [tolerance=±1% resistance=1k package=THT]
  10k = Resistor [tolerance=±1% resistance=1k package=THT]
  10k_2 = Resistor [tolerance=±1% resistance=1k package=THT]
  47k = Resistor [tolerance=±1% resistance=1k package=THT]
  10k_3 = Resistor [tolerance=±1% resistance=1k package=THT]
  47k_2 = Resistor [tolerance=±1% resistance=1k package=THT]
  4_7k_6 = Resistor [tolerance=±1% resistance=1k package=THT]
  4_7k_7 = Resistor [tolerance=±1% resistance=1k package=THT]
  10k_4 = Resistor [tolerance=±1% resistance=1k package=THT]
  4_7k_8 = Resistor [tolerance=±1% resistance=1k package=THT]
  10k_5 = Resistor [tolerance=±1% resistance=1k package=THT]
  IC3 = ULN2003A [package="DIP16 [THT]"]
  10k_6 = Resistor [tolerance=±1% resistance=1k package=THT]
  10k_7 = Resistor [tolerance=±1% resistance=1k package=THT]
  10k_8 = Resistor [tolerance=±1% resistance=1k package=THT]
  47k_3 = Resistor [tolerance=±1% resistance=1k package=THT]
  47k_4 = Resistor [tolerance=±1% resistance=1k package=THT]
  47k_5 = Resistor [tolerance=±1% resistance=1k package=THT]
  47k_6 = Resistor [tolerance=±1% resistance=1k package=THT]
  100k = Resistor [tolerance=±1% resistance=1k package=THT]
  SLOT9 = Lilypad Battery Connect  # not connected
  Part35 = Lilypad Battery Connect
  100k_2 = Resistor [tolerance=±1% resistance=1k package=THT]
  SLOT19 = Lilypad Battery Connect  # not connected
  SLOT18 = Lilypad Battery Connect  # not connected
  SLOT15 = Lilypad Battery Connect
  SLOT16 = Lilypad Battery Connect
  SLOT17 = Lilypad Battery Connect  # not connected
  SLOT11 = Lilypad Battery Connect
  SLOT13 = Lilypad Battery Connect  # not connected
  SLOT14 = Lilypad Battery Connect
  SLOT12 = Lilypad Battery Connect  # not connected
  SLOT10 = Lilypad Battery Connect  # not connected
  SLOT20 = Lilypad Battery Connect  # not connected
  4_7k_9 = Resistor [tolerance=±1% resistance=1k package=THT]
  4_7k_10 = Resistor [tolerance=±1% resistance=1k package=THT]
  4_7k_11 = Resistor [tolerance=±1% resistance=1k package=THT]
  4_7k_12 = Resistor [tolerance=±1% resistance=1k package=THT]
  150k = Resistor [tolerance=±1% resistance=1k package=THT]
  150k_2 = Resistor [tolerance=±1% resistance=1k package=THT]
  100k_3 = Resistor [tolerance=±1% resistance=1k package=THT]
  100k_4 = Resistor [tolerance=±1% resistance=1k package=THT]
  IC4 = ULN2003A [package="DIP16 [THT]"]
  Part41 = Lilypad Battery Connect
  Part42 = Lilypad Battery Connect
  Part44 = Lilypad Battery Connect
  150k_3 = Resistor [tolerance=±1% resistance=1k package=THT]
  100k_5 = Resistor [tolerance=±1% resistance=1k package=THT]
  150k_4 = Resistor [tolerance=±1% resistance=1k package=THT]
  Part45 = Lilypad Battery Connect
  Part46 = Lilypad Battery Connect
  Part47 = Lilypad Battery Connect
  Part48 = Lilypad Battery Connect
  Part49 = Lilypad Battery Connect
  Part50 = Lilypad Battery Connect
  Part51 = Lilypad Battery Connect
  Part52 = Lilypad Battery Connect
  Part53 = Lilypad Battery Connect
  100k_6 = Resistor [tolerance=±1% resistance=1k package=THT]
  4_7k_13 = Resistor [tolerance=±1% resistance=1k package=THT]
  4_7k_14 = Resistor [tolerance=±1% resistance=1k package=THT]
  47k_7 = Resistor [tolerance=±1% resistance=1k package=THT]
  47k_8 = Resistor [tolerance=±1% resistance=1k package=THT]
  10k_9 = Resistor [tolerance=±1% resistance=1k package=THT]
  4_7k_15 = Resistor [tolerance=±1% resistance=1k package=THT]
  4_7k_16 = Resistor [tolerance=±1% resistance=1k package=THT]
  10k_10 = Resistor [tolerance=±1% resistance=1k package=THT]
  LED7 = DUO LED RG [package="5 mm [THT]"]
  LED8 = DUO LED RG [package="5 mm [THT]"]
  LED9 = DUO LED RG [package="5 mm [THT]"]
  LED10 = DUO LED RG [package="5 mm [THT]"]
  LED11 = DUO LED RG [package="5 mm [THT]"]

nets:
  N1: Raspberry_Pi_2.3v3, IC2.Out_1
  N2: Raspberry_Pi_2.GIPO4, LED10.green_anode
  N3: Raspberry_Pi_2.GND, IC2.Out_3, 4_7k.Pin_1, 4_7k_2.Pin_1, 4_7k_5.Pin_1, 10k.Pin_1, 10k_3.Pin_1, 4_7k_6.Pin_1, 4_7k_7.Pin_1, 4_7k_8.Pin_1, LED9.common_cathode
  N4: Raspberry_Pi_2.GIPO17, IC2.Out_7
  N5: Raspberry_Pi_2.GIPO27, IC3.Out_7
  N6: Raspberry_Pi_2.GIPO22, LED7.green_anode
  N7: Raspberry_Pi_2.GIPO5, LED10.red_anode
  N8: Raspberry_Pi_2.GIPO6, LED9.green_anode
  N9: Raspberry_Pi_2.GIPO13, LED8.green_anode
  N10: Raspberry_Pi_2.GIPO19, LED9.red_anode
  N11: Raspberry_Pi_2.GIPO26, LED7.red_anode
  N12: Raspberry_Pi_2.GIPO21, LED11.red_anode
  N13: Raspberry_Pi_2.GIPO20, LED11.green_anode
  N14: Raspberry_Pi_2.GIPO16, LED8.red_anode
  N15: Raspberry_Pi_2.GIPO25, IC4.Out_7
  N16: Raspberry_Pi_2.GIPO24, IC3.Out_6
  N17: Raspberry_Pi_2.GIPO23, IC2.Out_5
  N18: Raspberry_Pi_2.GIPO18, IC2.Out_4
  N19: SLOT8.+, IC2.0V, 10k.Pin_0
  N20: SLOT5.+, IC2.In_5, 4_7k_2.Pin_0
  N21: SLOT1.+, 4_7k_6.Pin_0
  N22: SLOT4.+, IC2.In_4, 4_7k_8.Pin_0
  N23: Part25.-, 47k_2.Pin_1
  N24: Part25.+, 47k_2.Pin_0
  N25: Part26.-, 10k_2.Pin_1
  N26: Part26.+, 10k_2.Pin_0
  N27: Part28.-, 47k.Pin_1
  N28: Part28.+, 47k.Pin_0
  N29: Part29.-, 4_7k_4.Pin_1
  N30: Part29.+, 4_7k_4.Pin_0
  N31: Part30.-, 10k_5.Pin_1
  N32: Part30.+, 10k_5.Pin_0
  N33: Part31.-, 10k_4.Pin_1
  N34: Part31.+, 10k_4.Pin_0
  N35: Part32.-, 4_7k_3.Pin_1
  N36: Part32.+, 4_7k_3.Pin_0
  N37: IC2.In_2, 4_7k_7.Pin_0
  N38: IC2.In_3, 4_7k.Pin_0
  N39: IC2.In_6, 4_7k_5.Pin_0
  N40: IC2.In_7, 10k_3.Pin_0
  N41: IC3.In_1, 10k_6.Pin_0
  N42: IC3.In_2, 10k_7.Pin_0
  N43: IC3.In_3, 10k_8.Pin_0, SLOT11.+
  N44: IC3.In_4, 47k_3.Pin_0
  N45: IC3.In_5, 47k_4.Pin_0
  N46: IC3.In_6, 47k_5.Pin_0, SLOT14.+
  N47: IC3.In_7, 47k_6.Pin_0, SLOT15.+
  N48: IC3.0V, 100k.Pin_0, SLOT16.+
  N49: 100k.Pin_1, 4_7k_9.Pin_1, 4_7k_10.Pin_1, 4_7k_11.Pin_1, 4_7k_12.Pin_1, 150k.Pin_1, 150k_2.Pin_1, 100k_3.Pin_1, 100k_4.Pin_1
  N50: Part35.-, 100k_2.Pin_1
  N51: Part35.+, 100k_2.Pin_0
  N52: 4_7k_9.Pin_0, IC4.0V
  N53: 4_7k_10.Pin_0, IC4.In_7
  N54: 4_7k_11.Pin_0, IC4.In_6
  N55: 4_7k_12.Pin_0, IC4.In_5
  N56: 150k.Pin_0, IC4.In_4
  N57: 150k_2.Pin_0, IC4.In_3
  N58: 100k_3.Pin_0, IC4.In_2
  N59: 100k_4.Pin_0, IC4.In_1
  N60: Part41.-, 100k_5.Pin_1
  N61: Part41.+, 100k_5.Pin_0
  N62: Part42.-, 150k_3.Pin_1
  N63: Part42.+, 150k_3.Pin_0
  N64: Part44.-, 150k_4.Pin_1
  N65: Part44.+, 150k_4.Pin_0
  N66: Part45.-, 100k_6.Pin_1
  N67: Part45.+, 100k_6.Pin_0
  N68: Part46.-, 47k_7.Pin_1
  N69: Part46.+, 47k_7.Pin_0
  N70: Part47.-, 10k_9.Pin_1
  N71: Part47.+, 10k_9.Pin_0
  N72: Part48.-, 10k_10.Pin_1
  N73: Part48.+, 10k_10.Pin_0
  N74: Part49.-, 47k_8.Pin_1
  N75: Part49.+, 47k_8.Pin_0
  N76: Part50.-, 4_7k_15.Pin_1
  N77: Part50.+, 4_7k_15.Pin_0
  N78: Part51.-, 4_7k_13.Pin_1
  N79: Part51.+, 4_7k_13.Pin_0
  N80: Part52.-, 4_7k_14.Pin_1
  N81: Part52.+, 4_7k_14.Pin_0
  N82: Part53.-, 4_7k_16.Pin_1
  N83: Part53.+, 4_7k_16.Pin_0

notes:
  rodzaje klocków
  LED1
  LED2
  LED3
  LED4
  LED5
