# Fritzing sketch PIGMALION-v2019-04-25 (saved by Fritzing 0.9.3b)

parts:
  Raspberry_Pi_1 = Raspberry Pi 3 [part_number=RPI-3-V1.2]
  IC1 = ULN2003A [package="DIP16 [THT]"]
  SLOT12 = Lilypad Battery Connect
  SLOT11 = Lilypad Battery Connect  # not connected
  SLOT10 = Lilypad Battery Connect  # not connected
  SLOT9 = Lilypad Battery Connect
  SLOT16 = Lilypad Battery Connect  # not connected
  SLOT15 = Lilypad Battery Connect  # not connected
  SLOT13 = Lilypad Battery Connect
  SLOT14 = Lilypad Battery Connect  # not connected
  LED2 = DUO LED RG [package="5 mm [THT]"]
  LED3 = DUO LED RG [package="5 mm [THT]"]
  LED4 = DUO LED RG [package="5 mm [THT]"]
  LED5 = DUO LED RG [package="5 mm [THT]"]
  8_2k = Resistor [tolerance=±1% resistance=1k package=THT]
  10k = Resistor [tolerance=±1% resistance=1k package=THT]
  12k = Resistor [tolerance=±1% resistance=1k package=THT]
  22k = Resistor [tolerance=±1% resistance=1k package=THT]
  32k = Resistor [tolerance=±1% resistance=1k package=THT]
  39k = Resistor [tolerance=±1% resistance=1k package=THT]
  47k = Resistor [tolerance=±1% resistance=1k package=THT]
  56k = Resistor [tolerance=±1% resistance=1k package=THT]
  Part9 = Lilypad Battery Connect
  Part10 = Lilypad Battery Connect
  Part11 = Lilypad Battery Connect
  Part12 = Lilypad Battery Connect
  Part13 = Lilypad Battery Connect
  Part14 = Lilypad Battery Connect
  Part15 = Lilypad Battery Connect
  Part16 = Lilypad Battery Connect
  39k_2 = Resistor [tolerance=±1% resistance=1k package=THT]
  22k_2 = Resistor [tolerance=±1% resistance=1k package=THT]
  8_1k = Resistor [tolerance=±1% resistance=1k package=THT]
  56k_2 = Resistor [tolerance=±1% resistance=1k package=THT]
  10k_2 = Resistor [tolerance=±1% resistance=1k package=THT]
  12k_2 = Resistor [tolerance=±1% resistance=1k package=THT]
  32k_2 = Resistor [tolerance=±1% resistance=1k package=THT]
  47k_2 = Resistor [tolerance=±1% resistance=1k package=THT]
  Raspberry_Pi_2 = Raspberry Pi 3 [part_number=RPI-3-V1.2]
  SLOT8 = Lilypad Battery Connect
  SLOT5 = Lilypad Battery Connect
  SLOT6 = Lilypad Battery Connect  # not connected
  SLOT7 = Lilypad Battery Connect  # not connected
  SLOT1 = Lilypad Battery Connect
  SLOT3 = Lilypad Battery Connect  # not connected
  SLOT4 = Lilypad Battery Connect
  SLOT2 = Lilypad Battery Connect  # not connected
  Part25 = Lilypad Battery Connect
  Part26 = Lilypad Battery Connect
  Part27 = Lilypad Battery Connect
  Part28 = Lilypad Battery Connect
  Part29 = Lilypad Battery Connect
  Part30 = Lilypad Battery Connect
  Part31 = Lilypad Battery Connect
  Part32 = Lilypad Battery Connect
  IC2 = ULN2003A [package="DIP16 [THT]"]
  LED6 = DUO LED RG [package="5 mm [THT]"]
  LED7 = DUO LED RG [package="5 mm [THT]"]
  LED8 = DUO LED RG [package="5 mm [THT]"]
  LED9 = DUO LED RG [package="5 mm [THT]"]
  1_7k = Resistor [tolerance=±1% resistance=1k package=THT]
  3_9k = Resistor [tolerance=±1% resistance=1k package=THT]
  3k = Resistor [tolerance=±1% resistance=1k package=THT]
  1_3k = Resistor [tolerance=±1% resistance=1k package=THT]
  1k = Resistor [tolerance=±1% resistance=1k package=THT]
  3_9k_2 = Resistor [tolerance=±1% resistance=1k package=THT]
  6_7k = Resistor [tolerance=±1% resistance=1k package=THT]
  3k_2 = Resistor [tolerance=±1% resistance=1k package=THT]
  4_7k = Resistor [tolerance=±1% resistance=1k package=THT]
  4_7k_2 = Resistor [tolerance=±1% resistance=1k package=THT]
  1k_2 = Resistor [tolerance=±1% resistance=1k package=THT]
  1_3k_2 = Resistor [tolerance=±1% resistance=1k package=THT]
  2k = Resistor [tolerance=±1% resistance=1k package=THT]
  2k_2 = Resistor [tolerance=±1% resistance=1k package=THT]
  1_7k_2 = Resistor [tolerance=±1% resistance=1k package=THT]
  6_7k_2 = Resistor [tolerance=±1% resistance=1k package=THT]

nets:
  N1: Raspberry_Pi_1.3v3, IC1.Out_1
  N2: Raspberry_Pi_1.GND, IC1.Out_3, 8_2k.Pin_1, 56k.Pin_1
  N3: Raspberry_Pi_1.GIPO17, IC1.Out_7
  N4: Raspberry_Pi_1.GIPO6, LED3.red_anode
  N5: Raspberry_Pi_1.GIPO13, LED2.green_anode
  N6: Raspberry_Pi_1.GIPO19, LED3.green_anode
  N7: Raspberry_Pi_1.GIPO26, LED4.green_anode
  N8: Raspberry_Pi_1.GIPO21, LED5.red_anode
  N9: Raspberry_Pi_1.GIPO20, LED5.green_anode
  N10: Raspberry_Pi_1.GIPO16, LED2.red_anode
  N11: Raspberry_Pi_1.GIPO12, LED4.red_anode
  N12: Raspberry_Pi_1.GIPO24, IC1.Out_6
  N13: Raspberry_Pi_1.GIPO23, IC1.Out_5
  N14: Raspberry_Pi_1.GIPO18, IC1.Out_4
  N15: IC1.In_1, SLOT9.+, 8_2k.Pin_0
  N16: IC1.In_2, 10k.Pin_0
  N17: IC1.In_3, 12k.Pin_0
  N18: IC1.In_4, SLOT12.+, 22k.Pin_0
  N19: IC1.In_5, SLOT13.+, 32k.Pin_0
  N20: IC1.In_6, 39k.Pin_0
  N21: IC1.In_7, 47k.Pin_0
  N22: IC1.0V, 56k.Pin_0
  N23: Part9.-, 56k_2.Pin_1
  N24: Part9.+, 56k_2.Pin_0
  N25: Part10.-, 32k_2.Pin_1
  N26: Part10.+, 32k_2.Pin_0
  N27: Part11.-, 39k_2.Pin_1
  N28: Part11.+, 39k_2.Pin_0
  N29: Part12.-, 47k_2.Pin_1
  N30: Part12.+, 47k_2.Pin_0
  N31: Part13.-, 8_1k.Pin_1
  N32: Part13.+, 8_1k.Pin_0
  N33: Part14.-, 12k_2.Pin_1
  N34: Part14.+, 12k_2.Pin_0
  N35: Part15.-, 22k_2.Pin_1
  N36: Part15.+, 22k_2.Pin_0
  N37: Part16.-, 10k_2.Pin_1
  N38: Part16.+, 10k_2.Pin_0
  N39: Raspberry_Pi_2.3v3, IC2.Out_1
  N40: Raspberry_Pi_2.GND, IC2.Out_3, 1_7k.Pin_1, 3k.Pin_1, 3_9k_2.Pin_1, 6_7k.Pin_1, 4_7k_2.Pin_1, 1k_2.Pin_1, 1_3k_2.Pin_1, 2k_2.Pin_1
  N41: Raspberry_Pi_2.GIPO17, IC2.Out_7
  N42: Raspberry_Pi_2.GIPO6, LED7.red_anode
  N43: Raspberry_Pi_2.GIPO13, LED8.green_anode
  N44: Raspberry_Pi_2.GIPO19, LED7.green_anode
  N45: Raspberry_Pi_2.GIPO26, LED9.green_anode
  N46: Raspberry_Pi_2.GIPO21, LED6.red_anode
  N47: Raspberry_Pi_2.GIPO20, LED6.green_anode
  N48: Raspberry_Pi_2.GIPO16, LED8.red_anode
  N49: Raspberry_Pi_2.GIPO12, LED9.red_anode
  N50: Raspberry_Pi_2.GIPO24, IC2.Out_6
  N51: Raspberry_Pi_2.GIPO23, IC2.Out_5
  N52: Raspberry_Pi_2.GIPO15, IC2.Out_4
  N53: SLOT8.+, IC2.0V, 6_7k.Pin_0
  N54: SLOT5.+, IC2.In_5, 3k.Pin_0
  N55: SLOT1.+, IC2.In_1, 1k_2.Pin_0
  N56: SLOT4.+, IC2.In_4, 2k_2.Pin_0
  N57: Part25.-, 6_7k_2.Pin_1
  N58: Part25.+, 6_7k_2.Pin_0
  N59: Part26.-, 3k_2.Pin_1
  N60: Part26.+, 3k_2.Pin_0
  N61: Part27.-, 3_9k.Pin_1
  N62: Part27.+, 3_9k.Pin_0
  N63: Part28.-, 4_7k.Pin_1
  N64: Part28.+, 4_7k.Pin_0
  N65: Part29.-, 1k.Pin_1
  N66: Part29.+, 1k.Pin_0
  N67: Part30.-, 1_7k_2.Pin_1
  N68: Part30.+, 1_7k_2.Pin_0
  N69: Part31.-, 2k.Pin_1
  N70: Part31.+, 2k.Pin_0
  N71: Part32.-, 1_3k.Pin_1
  N72: Part32.+, 1_3k.Pin_0
  N73: IC2.In_2, 1_3k_2.Pin_0
  N74: IC2.In_3, 1_7k.Pin_0
  N75: IC2.In_6, 3_9k_2.Pin_0
  N76: IC2.In_7, 4_7k_2.Pin_0

notes:
  PYGMALION 1
  KLOCKI
  SLOTY
  PYGMALION 2
